// Logisim project Cleopatra_datapath_v2.circ as structural Verilog: 4 circuits, main circuit Data Path
module Data_Path (
  input  lcv,
  input  lnz,
  input  ce,
  input  rw,
  input  [2:0] alu_op,
  input  [2:0] write_reg,
  input  [2:0] read_reg,
  output C,
  output V,
  output N,
  output Z
);

  wire and_1_out, and_2_out, Clock_out, readdecoder_1_rdac, readdecoder_1_rdir, readdecoder_1_rdmdr,
       readdecoder_1_rdpc, readdecoder_1_rdrs, Reset_out, writedecoder_1_wrac, writedecoder_1_wrir,
       writedecoder_1_wrmar, writedecoder_1_wrmdr, writedecoder_1_wrpc, writedecoder_1_wrrs;
  wire [3:0] alu_1_flags;
  wire [7:0] AC_q, alu_1_c, controlled_buffer_2_out, controlled_buffer_4_out, IR_q, MAR_q, MDR_q,
       multiplexer_1_out, PC_q, ram_1_data, RS_q;

  // Probe on MAR_q
  // Probe on ram_1_data
  RAM ram_1 (.addr(MAR_q), .data(ram_1_data), .sel(ce), .clk(Clock_out), .ld(rw));  // open: clr
  assign ram_1_data = and_1_out ? alu_1_c : 8'bz;  // Controlled_Buffer controlled_buffer_1
  and and_1 (and_1_out, ce, ~rw);  // AND_Gate
  // Probe on multiplexer_1_out
  Multiplexer #(.width(8), .disabled(0), .enable("false")) multiplexer_1 (
    .in0(alu_1_c), .in1(ram_1_data), .out(multiplexer_1_out), .sel(and_2_out));
  and and_2 (and_2_out, ce, rw);
  WriteDecoder writedecoder_1 (
    .A(write_reg), .wrMAR(writedecoder_1_wrmar), .wrMDR(writedecoder_1_wrmdr), .wrIR(writedecoder_1_wrir),
    .wrPC(writedecoder_1_wrpc), .wrAC(writedecoder_1_wrac), .wrRS(writedecoder_1_wrrs));
  Button Reset (.out(Reset_out));
  Register MAR (.D(alu_1_c), .en(writedecoder_1_wrmar), .Q(MAR_q), .clk(Clock_out), .clr(Reset_out));
  Register MDR (.D(multiplexer_1_out), .en(writedecoder_1_wrmdr), .Q(MDR_q), .clk(Clock_out), .clr(Reset_out));
  Register IR (.D(alu_1_c), .en(writedecoder_1_wrir), .Q(IR_q), .clk(Clock_out), .clr(Reset_out));
  Register PC (.D(alu_1_c), .en(writedecoder_1_wrpc), .Q(PC_q), .clk(Clock_out), .clr(Reset_out));
  Register AC (.D(alu_1_c), .en(writedecoder_1_wrac), .Q(AC_q), .clk(Clock_out), .clr(Reset_out));
  Register RS (.D(alu_1_c), .en(writedecoder_1_wrrs), .Q(RS_q), .clk(Clock_out), .clr(Reset_out));
  ReadDecoder readdecoder_1 (
    .A(read_reg), .rdMDR(readdecoder_1_rdmdr), .rdIR(readdecoder_1_rdir), .rdPC(readdecoder_1_rdpc),
    .rdAC(readdecoder_1_rdac), .rdRS(readdecoder_1_rdrs));
  Button Clock (.out(Clock_out));
  assign controlled_buffer_2_out = readdecoder_1_rdmdr ? MDR_q : 8'bz;  // Controlled_Buffer controlled_buffer_2
  assign controlled_buffer_2_out = readdecoder_1_rdir ? IR_q : 8'bz;  // Controlled_Buffer controlled_buffer_3
  // Probe on controlled_buffer_2_out
  // Probe on controlled_buffer_4_out
  assign controlled_buffer_4_out = readdecoder_1_rdpc ? PC_q : 8'bz;  // Controlled_Buffer controlled_buffer_4
  assign controlled_buffer_4_out = readdecoder_1_rdac ? AC_q : 8'bz;  // Controlled_Buffer controlled_buffer_5
  assign controlled_buffer_4_out = readdecoder_1_rdrs ? RS_q : 8'bz;  // Controlled_Buffer controlled_buffer_6
  ALU alu_1 (
    .A(controlled_buffer_4_out), .B(controlled_buffer_2_out), .ALU_OP(alu_op), .C(alu_1_c),
    .Flags(alu_1_flags));
  // Probe on alu_1_c
  D_Flip_Flop u_C (.clk(Clock_out), .D(alu_1_flags[3]), .Q(C), .en(lcv), .reset(Reset_out));  // open: Qn, preset
  D_Flip_Flop u_V (.clk(Clock_out), .D(alu_1_flags[2]), .Q(V), .en(lcv), .reset(Reset_out));  // open: Qn, preset
  D_Flip_Flop u_N (.clk(Clock_out), .D(alu_1_flags[1]), .Q(N), .en(lnz), .reset(Reset_out));  // open: Qn, preset
  D_Flip_Flop u_Z (.clk(Clock_out), .D(alu_1_flags[0]), .Q(Z), .en(lnz), .reset(Reset_out));  // open: Qn, preset

  // Notes on the sheet:
  //   Write dec
  //   Read dec
  //   Status flags
endmodule

module ALU (
  input  [7:0] A,
  input  [7:0] B,
  input  [2:0] ALU_OP,
  output [3:0] Flags,
  output [7:0] C
);

  wire adder_1_cout, adder_2_cout, bitselector_1_out, bitselector_2_out, bitselector_3_out, nor_1_out,
       xor_1_out;
  wire [7:0] adder_1_out, adder_2_out, and_1_out, not_1_out, or_1_out;

  Adder adder_1 (.a(A), .b(B), .out(adder_1_out), .cout(adder_1_cout));  // open: cin
  Adder adder_2 (.a(A), .b(8'h1), .out(adder_2_out), .cout(adder_2_cout));  // open: cin
  assign not_1_out = ~A;  // NOT_Gate not_1, 8 bits wide
  assign or_1_out = A | B;  // OR_Gate or_1, 8 bits wide
  assign and_1_out = A & B;  // AND_Gate and_1, 8 bits wide
  or or_2 (Flags[3], adder_1_cout, adder_2_cout);
  BitSelector bitselector_1 (.in(B), .out(bitselector_1_out), .sel(3'b111));
  BitSelector bitselector_2 (.in(A), .out(bitselector_2_out), .sel(3'b111));
  and and_2 (Flags[2], nor_1_out, xor_1_out);
  nor nor_1 (nor_1_out, bitselector_1_out, bitselector_2_out);
  xor xor_1 (xor_1_out, bitselector_2_out, bitselector_3_out);
  BitSelector bitselector_3 (.in(C), .out(bitselector_3_out), .sel(3'b111));
  Multiplexer #(.select(3), .width(8), .disabled(0), .enable("false")) multiplexer_1 (
    .in0(adder_1_out), .in1(adder_2_out), .in2(not_1_out), .in4(B), .in5(or_1_out), .in6(and_1_out), .in7(A),
    .out(C), .sel(ALU_OP));  // open: in3
  nor nor_2 (Flags[0], C[7], C[6], C[5], C[4], C[3], C[2], C[1], C[0]);

  assign Flags[1] = C[7];

  // Notes on the sheet:
  //   Carry
  //   Overflow
  //   N
  //   Zero
endmodule

module ReadDecoder (
  input  [2:0] A,
  output rdMDR,
  output rdIR,
  output rdPC,
  output rdAC,
  output rdRS
);

  wire and_1_out, and_2_out, not_1_out, not_2_out, not_3_out, not_4_out, not_5_out, not_6_out;

  not not_1 (not_1_out, A[2]);
  not not_2 (not_2_out, A[1]);
  not not_3 (not_3_out, A[2]);
  not not_4 (not_4_out, A[0]);
  not not_5 (not_5_out, A[0]);
  not not_6 (not_6_out, A[1]);
  and and_1 (and_1_out, not_1_out, not_2_out, A[0]);
  and and_2 (and_2_out, A[2], A[1]);
  and and_3 (rdIR, not_3_out, A[1], not_4_out);
  and and_4 (rdPC, A[1], A[0]);
  and and_5 (rdAC, A[2], not_5_out);
  and and_6 (rdRS, A[2], not_6_out, A[0]);
  or or_1 (rdMDR, and_1_out, and_2_out);
endmodule

module WriteDecoder (
  input  [2:0] A,
  output wrMAR,
  output wrMDR,
  output wrIR,
  output wrPC,
  output wrAC,
  output wrRS
);

  wire and_2_out, and_3_out, and_5_out, and_6_out, not_1_out, not_2_out, not_3_out, not_4_out, not_5_out,
       not_6_out, not_7_out, not_8_out, not_9_out, not_10_out, not_11_out, not_12_out, not_13_out;

  not not_1 (not_1_out, A[2]);
  not not_2 (not_2_out, A[1]);
  not not_3 (not_3_out, A[0]);
  not not_4 (not_4_out, A[2]);
  not not_5 (not_5_out, A[1]);
  not not_6 (not_6_out, A[0]);
  not not_7 (not_7_out, A[2]);
  not not_8 (not_8_out, A[0]);
  not not_9 (not_9_out, A[2]);
  not not_10 (not_10_out, A[0]);
  not not_11 (not_11_out, A[1]);
  not not_12 (not_12_out, A[0]);
  not not_13 (not_13_out, A[1]);
  and and_1 (wrMAR, not_1_out, not_2_out, not_3_out);
  and and_2 (and_2_out, not_4_out, not_5_out, A[0]);
  or or_1 (wrMDR, and_2_out, and_3_out);
  and and_3 (and_3_out, A[2], A[1], not_6_out);
  and and_4 (wrIR, not_7_out, A[1], not_8_out);
  and and_5 (and_5_out, not_9_out, A[1], A[0]);
  or or_2 (wrPC, and_5_out, and_6_out);
  and and_6 (and_6_out, A[2], A[1], not_10_out);
  and and_7 (wrAC, A[2], not_11_out, not_12_out);
  and and_8 (wrRS, A[2], not_13_out, A[0]);
endmodule
