// Logisim project Cleopatra_v2_with_block.circ as structural Verilog: 5 circuits, main circuit main
module main (
);

  wire and_1_out, and_2_out, button_1_out, C, CE, Clock, clock_1_out, LCV, LNZ, N, readdecoder_1_rdac,
       readdecoder_1_rdir, readdecoder_1_rdmdr, readdecoder_1_rdpc, readdecoder_1_rdrs, Reset, RW, V,
       writedecoder_1_wrac, writedecoder_1_wrir, writedecoder_1_wrmar, writedecoder_1_wrmdr,
       writedecoder_1_wrpc, writedecoder_1_wrrs, Z;
  wire [2:0] ALU, READ, WRITE;
  wire [3:0] alu_1_flags;
  wire [7:0] AC_q, alu_1_c, CONTROL, controlled_buffer_2_out, controlled_buffer_4_out, MAR_q, MDR_q,
       multiplexer_1_out, PC_q, ram_1_data, RS_q;

  // Probe on MAR_q
  Clock clock_1 (.out(clock_1_out));
  Button button_1 (.out(button_1_out));
  or or_1 (Clock, clock_1_out, button_1_out);
  Button button_2 (.out(Reset));
  // Probe on ram_1_data
  RAM ram_1 (.addr(MAR_q), .data(ram_1_data), .sel(CE), .clk(Clock), .ld(RW));  // open: clr
  assign ram_1_data = and_1_out ? alu_1_c : 8'bz;  // Controlled_Buffer controlled_buffer_1
  and and_1 (and_1_out, CE, ~RW);  // AND_Gate
  // Probe on multiplexer_1_out
  Multiplexer #(.width(8), .disabled(0), .enable("false")) multiplexer_1 (
    .in0(alu_1_c), .in1(ram_1_data), .out(multiplexer_1_out), .sel(and_2_out));
  and and_2 (and_2_out, CE, RW);
  WriteDecoder writedecoder_1 (
    .A(WRITE), .wrMAR(writedecoder_1_wrmar), .wrMDR(writedecoder_1_wrmdr), .wrIR(writedecoder_1_wrir),
    .wrPC(writedecoder_1_wrpc), .wrAC(writedecoder_1_wrac), .wrRS(writedecoder_1_wrrs));
  // Probe on WRITE
  Register MAR (.D(alu_1_c), .en(writedecoder_1_wrmar), .Q(MAR_q), .clk(Clock), .clr(Reset));
  Register MDR (.D(multiplexer_1_out), .en(writedecoder_1_wrmdr), .Q(MDR_q), .clk(Clock), .clr(Reset));
  Register IR (.D(alu_1_c), .en(writedecoder_1_wrir), .Q(CONTROL), .clk(Clock), .clr(Reset));
  Register PC (.D(alu_1_c), .en(writedecoder_1_wrpc), .Q(PC_q), .clk(Clock), .clr(Reset));
  Register AC (.D(alu_1_c), .en(writedecoder_1_wrac), .Q(AC_q), .clk(Clock), .clr(Reset));
  Register RS (.D(alu_1_c), .en(writedecoder_1_wrrs), .Q(RS_q), .clk(Clock), .clr(Reset));
  ReadDecoder readdecoder_1 (
    .A(READ), .rdMDR(readdecoder_1_rdmdr), .rdIR(readdecoder_1_rdir), .rdPC(readdecoder_1_rdpc),
    .rdAC(readdecoder_1_rdac), .rdRS(readdecoder_1_rdrs));
  assign controlled_buffer_2_out = readdecoder_1_rdmdr ? MDR_q : 8'bz;  // Controlled_Buffer controlled_buffer_2
  // Probe on READ
  // Probe on controlled_buffer_2_out
  assign controlled_buffer_2_out = readdecoder_1_rdir ? CONTROL : 8'bz;  // Controlled_Buffer controlled_buffer_3
  // Probe on controlled_buffer_4_out
  assign controlled_buffer_4_out = readdecoder_1_rdpc ? PC_q : 8'bz;  // Controlled_Buffer controlled_buffer_4
  assign controlled_buffer_4_out = readdecoder_1_rdac ? AC_q : 8'bz;  // Controlled_Buffer controlled_buffer_5
  assign controlled_buffer_4_out = readdecoder_1_rdrs ? RS_q : 8'bz;  // Controlled_Buffer controlled_buffer_6
  ALU alu_1 (.A(controlled_buffer_4_out), .B(controlled_buffer_2_out), .ALU_OP(ALU), .C(alu_1_c), .Flags(alu_1_flags));
  // Probe on ALU
  // Probe on alu_1_c
  D_Flip_Flop u_C (.clk(Clock), .D(alu_1_flags[3]), .Q(C), .en(LCV), .reset(Reset));  // open: Qn, preset
  D_Flip_Flop u_V (.clk(Clock), .D(alu_1_flags[2]), .Q(V), .en(LCV), .reset(Reset));  // open: Qn, preset
  D_Flip_Flop u_N (.clk(Clock), .D(alu_1_flags[1]), .Q(N), .en(LNZ), .reset(Reset));  // open: Qn, preset
  D_Flip_Flop u_Z (.clk(Clock), .D(alu_1_flags[0]), .Q(Z), .en(LNZ), .reset(Reset));  // open: Qn, preset
  ControlBlock controlblock_1 (
    .WRITE(WRITE), .READ(READ), .ALU(ALU), .CE(CE), .RW(RW), .LNZ(LNZ), .LCV(LCV), .in_7(CONTROL),
    .in_1(Reset), .C(C), .V(V), .N(N), .Z(Z), .in_2(Clock));

  // Other names for the same wires on the sheet: RST4 = Reset

  // Notes on the sheet:
  //   Write dec
  //   Read dec
  //   Mateus Piotroski Neis
  //   Gabriel de Jesus Coelho da Silva
  //   Status flags
endmodule

module ALU (
  input  [7:0] A,
  input  [7:0] B,
  input  [2:0] ALU_OP,
  output [3:0] Flags,
  output [7:0] C
);

  wire adder_1_cout, adder_2_cout, bitselector_1_out, bitselector_2_out, bitselector_3_out, nor_1_out,
       xor_1_out;
  wire [7:0] adder_1_out, adder_2_out, and_1_out, not_1_out, or_1_out;

  Adder adder_1 (.a(A), .b(B), .out(adder_1_out), .cout(adder_1_cout));  // open: cin
  Adder adder_2 (.a(A), .b(8'h1), .out(adder_2_out), .cout(adder_2_cout));  // open: cin
  assign not_1_out = ~A;  // NOT_Gate not_1, 8 bits wide
  assign or_1_out = A | B;  // OR_Gate or_1, 8 bits wide
  assign and_1_out = A & B;  // AND_Gate and_1, 8 bits wide
  or or_2 (Flags[3], adder_1_cout, adder_2_cout);
  BitSelector bitselector_1 (.in(B), .out(bitselector_1_out), .sel(3'b111));
  BitSelector bitselector_2 (.in(A), .out(bitselector_2_out), .sel(3'b111));
  and and_2 (Flags[2], nor_1_out, xor_1_out);
  xor xor_1 (xor_1_out, bitselector_2_out, bitselector_3_out);
  nor nor_1 (nor_1_out, bitselector_1_out, bitselector_2_out);
  BitSelector bitselector_3 (.in(C), .out(bitselector_3_out), .sel(3'b111));
  Multiplexer #(.select(3), .width(8), .disabled(0), .enable("false")) multiplexer_1 (
    .in0(adder_1_out), .in1(adder_2_out), .in2(not_1_out), .in4(B), .in5(or_1_out), .in6(and_1_out), .in7(A),
    .out(C), .sel(ALU_OP));  // open: in3
  nor nor_2 (Flags[0], C[7], C[6], C[5], C[4], C[3], C[2], C[1], C[0]);

  assign Flags[1] = C[7];

  // Notes on the sheet:
  //   Carry
  //   Overflow
  //   N
  //   Zero
  //   000 a + b
  //   001 a + 1
  //   010 not a
  //   011 nop
  //   101 a or b
  //   100 passa b
  //   110 a and b
  //   111 passa a
endmodule

module ReadDecoder (
  input  [2:0] A,
  output rdMDR,
  output rdIR,
  output rdPC,
  output rdAC,
  output rdRS
);

  wire and_1_out, and_2_out, not_1_out, not_2_out, not_3_out, not_4_out, not_5_out, not_6_out;

  not not_1 (not_1_out, A[2]);
  not not_2 (not_2_out, A[1]);
  not not_3 (not_3_out, A[2]);
  not not_4 (not_4_out, A[0]);
  not not_5 (not_5_out, A[0]);
  not not_6 (not_6_out, A[1]);
  and and_1 (and_1_out, not_1_out, not_2_out, A[0]);
  and and_2 (and_2_out, A[2], A[1]);
  and and_3 (rdIR, not_3_out, A[1], not_4_out);
  and and_4 (rdPC, A[1], A[0]);
  and and_5 (rdAC, A[2], not_5_out);
  and and_6 (rdRS, A[2], not_6_out, A[0]);
  or or_1 (rdMDR, and_1_out, and_2_out);

  // Notes on the sheet:
  //   000 NOP
  //   001 rdMDR
  //   010 rdIR
  //   011 rdPC
  //   100 rdAC
  //   101 rdRS
  //   110 rdMDR rdAC
  //   111 rdMDR rdPC
endmodule

module WriteDecoder (
  input  [2:0] A,
  output wrMAR,
  output wrMDR,
  output wrIR,
  output wrPC,
  output wrAC,
  output wrRS
);

  wire and_2_out, and_3_out, and_5_out, and_6_out, not_1_out, not_2_out, not_3_out, not_4_out, not_5_out,
       not_6_out, not_7_out, not_8_out, not_9_out, not_10_out, not_11_out, not_12_out, not_13_out;

  not not_1 (not_1_out, A[2]);
  not not_2 (not_2_out, A[1]);
  not not_3 (not_3_out, A[0]);
  not not_4 (not_4_out, A[2]);
  not not_5 (not_5_out, A[1]);
  not not_6 (not_6_out, A[0]);
  not not_7 (not_7_out, A[2]);
  not not_8 (not_8_out, A[0]);
  not not_9 (not_9_out, A[2]);
  not not_10 (not_10_out, A[0]);
  not not_11 (not_11_out, A[1]);
  not not_12 (not_12_out, A[0]);
  not not_13 (not_13_out, A[1]);
  and and_1 (wrMAR, not_1_out, not_2_out, not_3_out);
  and and_2 (and_2_out, not_4_out, not_5_out, A[0]);
  or or_1 (wrMDR, and_2_out, and_3_out);
  and and_3 (and_3_out, A[2], A[1], not_6_out);
  and and_4 (wrIR, not_7_out, A[1], not_8_out);
  and and_5 (and_5_out, not_9_out, A[1], A[0]);
  or or_2 (wrPC, and_5_out, and_6_out);
  and and_6 (and_6_out, A[2], A[1], not_10_out);
  and and_7 (wrAC, A[2], not_11_out, not_12_out);
  and and_8 (wrRS, A[2], not_13_out, A[0]);

  // Notes on the sheet:
  //   000 wrMAR
  //   001 wrMDR
  //   010 wrIR
  //   011 wrPC
  //   100 wrAC
  //   101 wrRS
  //   111 NOP
  //   110 wrMDR wrPC
endmodule

module ControlBlock (
  input  in_1,
  input  in_2,
  input  C,
  input  V,
  input  N,
  input  Z,
  input  [7:0] in_7,
  output [2:0] WRITE,
  output [2:0] READ,
  output [2:0] ALU,
  output CE,
  output RW,
  output LNZ,
  output LCV
);

  wire and_1_out, and_2_out, and_3_out, and_4_out, and_5_out, and_6_out, and_7_out, and_8_out, and_9_out,
       and_10_out, and_11_out, and_13_out, and_14_out, and_15_out, and_16_out, and_17_out, and_18_out,
       and_20_out, and_21_out, and_22_out, and_23_out, and_25_out, and_26_out, and_27_out, and_30_out,
       and_31_out, and_32_out, and_33_out, and_34_out, and_35_out, and_36_out, and_37_out, and_38_out,
       and_39_out, and_40_out, and_41_out, B0, B1, B2, B3, B4, B5, B6, B7, B8, B9, B10, decoder_2_out0,
       decoder_2_out1, decoder_2_out2, decoder_2_out3, decoder_3_out0, decoder_3_out2, decoder_3_out4,
       decoder_3_out5, decoder_3_out6, decoder_3_out7, decoder_3_out8, decoder_3_out9, decoder_3_out10,
       decoder_3_out11, decoder_3_out12, decoder_3_out13, decoder_3_out14, HLT, not_1_out, or_15_out,
       or_16_out, or_17_out, or_18_out, or_19_out, or_20_out, or_22_out, or_23_out, or_24_out, or_25_out,
       or_26_out, or_27_out, or_28_out, or_29_out, or_30_out, RST, RST1, RST2, RST3, RST5;
  wire [2:0] or_14_out;
  wire [3:0] adder_1_out, register_1_q;

  or or_1 (WRITE[0], and_7_out, and_9_out, and_8_out, and_23_out, and_6_out, and_4_out, and_16_out);
  or or_2 (WRITE[1], and_23_out, B2, and_16_out, and_7_out, or_16_out, and_8_out);
  or or_3 (WRITE[2], and_9_out, and_11_out, and_23_out, or_16_out, and_10_out);
  or or_4 (READ[0], or_16_out, or_17_out, and_5_out, and_8_out, and_7_out, and_17_out, and_9_out, and_16_out, B2, and_2_out);
  or or_5 (READ[1], or_16_out, and_11_out, and_8_out, or_17_out, and_17_out, and_9_out);
  or or_6 (READ[2], and_17_out, and_23_out, and_11_out, and_10_out, and_16_out, and_8_out);
  or or_7 (ALU[0], and_23_out, and_14_out, and_16_out, or_16_out, or_17_out, and_9_out);
  or or_8 (ALU[1], and_23_out, and_15_out, and_16_out, or_17_out, and_10_out, and_9_out);
  or or_9 (ALU[2], and_9_out, and_5_out, and_15_out, and_14_out, and_13_out, B2, and_1_out, or_17_out, and_23_out, and_7_out, and_16_out);
  or or_10 (CE, and_23_out, and_6_out, and_4_out, or_16_out);
  or or_11 (RW, and_4_out, and_6_out, or_16_out);
  or or_12 (LNZ, and_11_out, and_10_out);
  or or_13 (or_14_out[1], and_22_out, and_3_out, and_25_out);
  and and_1 (and_1_out, and_2_out, ~and_33_out);  // AND_Gate
  not not_1 (not_1_out, HLT);
  Adder #(.width(4)) adder_1 (.a(register_1_q), .b({1'b0, or_14_out}), .out(adder_1_out), .cin(1'b1));  // open: cout
  or or_14 (or_14_out[0], and_25_out, and_26_out);
  and and_2 (and_2_out, or_15_out, or_22_out);
  Register #(.width(4), .trigger("falling")) register_1 (
    .D(adder_1_out), .en(not_1_out), .Q(register_1_q), .clk(in_2), .clr(RST));
  or or_15 (or_15_out, B5, B7);
  and and_3 (and_3_out, B5, or_18_out);
  or or_16 (or_16_out, B1, and_21_out);
  Decoder #(.select(4)) decoder_1 (
    .out0(B0), .out1(B1), .out2(B2), .out3(B3), .out4(B4), .out5(B5), .out6(B6), .out7(B7), .out8(B8),
    .out9(B9), .out10(B10), .sel(register_1_q), .en(1'b1));  // open: out11, out12, out13, out14, out15
  and and_4 (and_4_out, and_18_out, ~and_23_out);  // AND_Gate
  and and_5 (and_5_out, B6, or_25_out);
  and and_6 (and_6_out, or_25_out, B7);
  and and_7 (and_7_out, B8, or_25_out);
  and and_8 (and_8_out, B8, and_37_out);
  and and_9 (and_9_out, B5, decoder_3_out12);
  and and_10 (and_10_out, B3, decoder_3_out0);
  or or_17 (or_17_out, and_20_out, B0);
  and and_11 (and_11_out, B9, or_28_out);
  and and_12 (LCV, B9, decoder_3_out5);
  and and_13 (and_13_out, B9, decoder_3_out4);
  and and_14 (and_14_out, B9, decoder_3_out6);
  and and_15 (and_15_out, B9, decoder_3_out7);
  and and_16 (and_16_out, B3, decoder_3_out13);
  and and_17 (and_17_out, and_33_out, B5);
  and and_18 (and_18_out, or_20_out, or_28_out);
  or or_18 (or_18_out, and_27_out, or_24_out);
  and and_19 (RST5, B4, or_19_out);
  and and_20 (and_20_out, B3, or_27_out);
  and and_21 (and_21_out, B4, or_27_out);
  and and_22 (and_22_out, B6, or_23_out);
  and and_23 (and_23_out, or_28_out, decoder_3_out2, B8);
  or or_19 (or_19_out, decoder_3_out0, decoder_3_out13);
  and and_24 (or_14_out[2], B4, and_30_out);
  or or_20 (or_20_out, B6, and_34_out);
  and and_25 (and_25_out, B4, ~decoder_3_out12, or_24_out);  // AND_Gate
  and and_26 (and_26_out, B4, ~decoder_3_out12, and_36_out);  // AND_Gate
  and and_27 (and_27_out, decoder_3_out2, decoder_2_out1);
  and and_28 (RST2, B9, or_26_out);
  and and_29 (RST1, B10, or_28_out);
  or or_21 (RST, RST1, RST2, RST5, RST3, in_1);
  or or_22 (or_22_out, and_31_out, and_33_out, and_32_out);
  or or_23 (or_23_out, and_31_out, and_33_out);
  or or_24 (or_24_out, and_35_out, and_37_out);
  or or_25 (or_25_out, and_35_out, and_36_out);
  or or_26 (or_26_out, decoder_3_out2, or_29_out);
  or or_27 (or_27_out, decoder_3_out2, decoder_3_out4, decoder_3_out5, decoder_3_out6, decoder_3_out7, decoder_3_out8, decoder_3_out9, decoder_3_out10, decoder_3_out11, decoder_3_out12, decoder_3_out14);
  or or_28 (or_28_out, decoder_3_out7, decoder_3_out6, decoder_3_out5, decoder_3_out4, decoder_3_out2);
  and and_30 (and_30_out, decoder_2_out0, or_28_out);
  and and_31 (and_31_out, decoder_2_out1, or_28_out);
  and and_32 (and_32_out, decoder_2_out2, or_28_out);
  and and_33 (and_33_out, decoder_2_out3, or_28_out);
  and and_34 (and_34_out, decoder_2_out2, B8);
  and and_35 (and_35_out, decoder_2_out1, or_29_out);
  and and_36 (and_36_out, decoder_2_out2, or_29_out);
  and and_37 (and_37_out, decoder_2_out3, or_29_out);
  or or_29 (or_29_out, decoder_3_out8, decoder_3_out9, decoder_3_out10, decoder_3_out11, decoder_3_out12, decoder_3_out14);
  or or_30 (or_30_out, B6, B7, B8);
  Decoder #(.select(2)) decoder_2 (
    .out0(decoder_2_out0), .out1(decoder_2_out1), .out2(decoder_2_out2), .out3(decoder_2_out3),
    .sel(in_7[3:2]), .en(1'b1));
  Decoder #(.select(4)) decoder_3 (
    .out0(decoder_3_out0), .out2(decoder_3_out2), .out4(decoder_3_out4), .out5(decoder_3_out5),
    .out6(decoder_3_out6), .out7(decoder_3_out7), .out8(decoder_3_out8), .out9(decoder_3_out9),
    .out10(decoder_3_out10), .out11(decoder_3_out11), .out12(decoder_3_out12), .out13(decoder_3_out13),
    .out14(decoder_3_out14), .out15(HLT), .sel(in_7[7:4]), .en(1'b1));  // open: out1, out3
  and and_38 (and_38_out, ~C, or_30_out, decoder_3_out9);  // AND_Gate
  and and_39 (and_39_out, ~N, or_30_out, decoder_3_out10);  // AND_Gate
  and and_40 (and_40_out, ~Z, or_30_out, decoder_3_out11);  // AND_Gate
  and and_41 (and_41_out, ~V, or_30_out, decoder_3_out14);  // AND_Gate
  or or_31 (RST3, and_38_out, and_39_out, and_40_out, and_41_out);

  // Notes on the sheet:
  //   NOT
  //   RTS
  //   SAIDA 9
  //   00 IMEDIATO
  //   01 DIRETO
  //   10 INDIRETO
  //   11 RELATIVO
  //   0000 NOT
  //   0001 NOP
  //   0010 STA
  //   0011 NOP
  //   0100 LDA
  //   0101 ADD
  //   0110 OR
  //   0111 AND
  //   1000 JMP
  //   1001 JC
  //   1010 JN
  //   1011 JZ
  //   1100 JSR
  //   1101 RTS
  //   1110 JV
  //   1111 HLT
endmodule
