// Logisim project MIPS Monocycle-jump-Terminal.circ as structural Verilog: 5 circuits, main circuit main
module main (
);

  wire addr_9, alu_1_zero, ALUSrc, and_1_out, and_2_out, and_3_out, Branch, clk, clk_out, clock_1_out, Jump,
       MemRead, MemToReg, MemWrite, RegDst, RegWrite, rst;
  wire [1:0] alu_1_result, ALUop, PC_q;
  wire [2:0] alucontrol_1_operation;
  wire [4:0] multiplexer_1_out;
  wire [5:0] rom_1_data;
  wire [6:0] alu_1_result_2, registerfile_1_readdata2;
  wire [7:0] PC_q_2;
  wire [25:0] rom_1_data_2;
  wire [31:0] adder_1_out, adder_2_out, bit_extender_1_out, multiplexer_2_out, multiplexer_3_out,
       multiplexer_4_out, multiplexer_5_out, ram_1_data, registerfile_1_readdata1, shifter_1_out;
  wire [31:7] registerfile_1_readdata2_2;
  wire [31:10] alu_1_result_3, PC_q_3;

  Button u_rst (.out(rst));
  Button u_clk (.out(clk_out));
  Clock clock_1 (.out(clock_1_out));
  Register #(.width(32)) PC (.D(multiplexer_4_out), .Q({PC_q_3, PC_q_2, PC_q}), .clk(clk), .clr(rst));  // open: en
  or or_1 (clk, clk_out, clock_1_out);
  Adder #(.width(32)) adder_1 (.a(32'h4), .b({PC_q_3, PC_q_2, PC_q}), .out(adder_1_out));  // open: cin, cout
  // Probe on rom_1_data
  ROM #(.dataWidth(32)) rom_1 (.addr(PC_q_2), .data({rom_1_data, rom_1_data_2}));  // open: sel
  ControlPath controlpath_1 (
    .Opcode(rom_1_data), .RegDst(RegDst), .ALUSrc(ALUSrc), .MemToReg(MemToReg), .RegWrite(RegWrite),
    .MemRead(MemRead), .MemWrite(MemWrite), .Branch(Branch), .ALUop(ALUop), .Jump(Jump));
  Multiplexer #(.width(5), .disabled(0), .enable("false")) multiplexer_1 (
    .in0(rom_1_data_2[20:16]), .in1(rom_1_data_2[15:11]), .out(multiplexer_1_out), .sel(RegDst));
  assign bit_extender_1_out = {{16{rom_1_data_2[15]}}, rom_1_data_2[15:0]};  // Bit_Extender bit_extender_1
  RegisterFile registerfile_1 (
    .ReadRegister1(rom_1_data_2[25:21]), .ReadRegister2(rom_1_data_2[20:16]),
    .WriteRegister(multiplexer_1_out), .WriteData(multiplexer_5_out), .ReadData1(registerfile_1_readdata1),
    .ReadData2({registerfile_1_readdata2_2, registerfile_1_readdata2}), .RegWrite(RegWrite), .Clock(clk),
    .Reset(rst));
  // Probe on registerfile_1_readdata2
  TTY #(.rows(5)) tty_1 (.data(registerfile_1_readdata2), .clk(clk), .we(and_1_out), .clr(rst));
  and and_1 (and_1_out, addr_9, MemWrite);
  Shifter #(.width(32)) shifter_1 (.in(bit_extender_1_out), .\dist (5'b00010), .out(shifter_1_out));
  ALU alu_1 (
    .op1(registerfile_1_readdata1), .op2(multiplexer_2_out), .Zero(alu_1_zero),
    .Result({alu_1_result_3, addr_9, alu_1_result_2, alu_1_result}), .operation(alucontrol_1_operation));
  Multiplexer #(.width(32), .disabled(0), .enable("false")) multiplexer_2 (
    .in0({registerfile_1_readdata2_2, registerfile_1_readdata2}), .in1(bit_extender_1_out),
    .out(multiplexer_2_out), .sel(ALUSrc));
  ALUControl alucontrol_1 (.funct(rom_1_data_2[5:0]), .operation(alucontrol_1_operation), .ALUop(ALUop));
  Adder #(.width(32)) adder_2 (.a(adder_1_out), .b(shifter_1_out), .out(adder_2_out));  // open: cin, cout
  Multiplexer #(.width(32), .disabled(0), .enable("false")) multiplexer_3 (
    .in0(adder_1_out), .in1(adder_2_out), .out(multiplexer_3_out), .sel(and_2_out));
  and and_2 (and_2_out, Branch, alu_1_zero);
  and and_3 (and_3_out, ~addr_9, MemWrite);  // AND_Gate
  Multiplexer #(.width(32), .disabled(0), .enable("false")) multiplexer_4 (
    .in0({adder_1_out[31:28], rom_1_data_2, 2'b00}), .in1(multiplexer_3_out), .out(multiplexer_4_out),
    .sel(Jump));
  RAM #(.dataWidth(32), .bus("separate")) ram_1 (
    .addr({addr_9, alu_1_result_2}), .din({registerfile_1_readdata2_2, registerfile_1_readdata2}),
    .data(ram_1_data), .str(and_3_out), .clk(clk), .ld(MemRead));  // open: sel, clr
  Multiplexer #(.width(32), .disabled(0), .enable("false")) multiplexer_5 (
    .in0(ram_1_data), .in1({alu_1_result_3, addr_9, alu_1_result_2, alu_1_result}), .out(multiplexer_5_out),
    .sel(MemToReg));

  // Notes on the sheet:
  //   1 KByte
  //   # terminal.asm
  //   addiu $8, $0, 512
  //   addiu $9, $0, '0'
  //   loop: sw $9, 0($8)
  //   addiu $9, $9, 1
  //   j loop
  //   contents of rom_1 (hex, n*v repeats v):
  //   24080200 24090030 ad090000 25290001 8100002
  //   rt
  //   rd
  //   Shifter
  //   Memory map (1 KByte)
  //   0:511 - Data memory
  //   512:1023 - Terminal
endmodule

module RegisterFile (
  input  [4:0] ReadRegister1,
  input  [4:0] ReadRegister2,
  input  RegWrite,
  input  [4:0] WriteRegister,
  input  [31:0] WriteData,
  input  Clock,
  input  Reset,
  output [31:0] ReadData1,
  output [31:0] ReadData2
);

  wire decoder_1_out0, decoder_1_out1, decoder_1_out2, decoder_1_out3, decoder_1_out4, decoder_1_out5,
       decoder_1_out6, decoder_1_out7, decoder_1_out8, decoder_1_out9, decoder_1_out10, decoder_1_out11,
       decoder_1_out12, decoder_1_out13, decoder_1_out14, decoder_1_out15, decoder_1_out16, decoder_1_out17,
       decoder_1_out18, decoder_1_out19, decoder_1_out20, decoder_1_out21, decoder_1_out22, decoder_1_out23,
       decoder_1_out24, decoder_1_out25, decoder_1_out26, decoder_1_out27, decoder_1_out28, decoder_1_out29,
       decoder_1_out30, decoder_1_out31;
  wire [31:0] R0_q, register_1_q, register_2_q, register_3_q, register_4_q, register_5_q, register_6_q,
       register_7_q, register_8_q, register_9_q, register_10_q, register_11_q, register_12_q, register_13_q,
       register_14_q, register_15_q, register_16_q, register_17_q, register_18_q, register_19_q,
       register_20_q, register_21_q, register_22_q, register_23_q, register_24_q, register_25_q,
       register_26_q, register_27_q, register_28_q, register_29_q, register_30_q, register_31_q;

  Decoder #(.select(5), .disabled(0)) decoder_1 (
    .out0(decoder_1_out0), .out1(decoder_1_out1), .out2(decoder_1_out2), .out3(decoder_1_out3),
    .out4(decoder_1_out4), .out5(decoder_1_out5), .out6(decoder_1_out6), .out7(decoder_1_out7),
    .out8(decoder_1_out8), .out9(decoder_1_out9), .out10(decoder_1_out10), .out11(decoder_1_out11),
    .out12(decoder_1_out12), .out13(decoder_1_out13), .out14(decoder_1_out14), .out15(decoder_1_out15),
    .out16(decoder_1_out16), .out17(decoder_1_out17), .out18(decoder_1_out18), .out19(decoder_1_out19),
    .out20(decoder_1_out20), .out21(decoder_1_out21), .out22(decoder_1_out22), .out23(decoder_1_out23),
    .out24(decoder_1_out24), .out25(decoder_1_out25), .out26(decoder_1_out26), .out27(decoder_1_out27),
    .out28(decoder_1_out28), .out29(decoder_1_out29), .out30(decoder_1_out30), .out31(decoder_1_out31),
    .sel(WriteRegister), .en(RegWrite));
  Register #(.width(32)) R0 (.D(WriteData), .en(1'b0), .Q(R0_q), .clk(Clock), .clr(Reset));
  Register #(.width(32)) register_1 (.D(WriteData), .en(decoder_1_out1), .Q(register_1_q), .clk(Clock), .clr(Reset));
  Register #(.width(32)) register_2 (.D(WriteData), .en(decoder_1_out2), .Q(register_2_q), .clk(Clock), .clr(Reset));
  Register #(.width(32)) register_3 (.D(WriteData), .en(decoder_1_out3), .Q(register_3_q), .clk(Clock), .clr(Reset));
  Register #(.width(32)) register_4 (.D(WriteData), .en(decoder_1_out4), .Q(register_4_q), .clk(Clock), .clr(Reset));
  Register #(.width(32)) register_5 (.D(WriteData), .en(decoder_1_out5), .Q(register_5_q), .clk(Clock), .clr(Reset));
  Register #(.width(32)) register_6 (.D(WriteData), .en(decoder_1_out6), .Q(register_6_q), .clk(Clock), .clr(Reset));
  Register #(.width(32)) register_7 (.D(WriteData), .en(decoder_1_out7), .Q(register_7_q), .clk(Clock), .clr(Reset));
  Register #(.width(32)) register_8 (.D(WriteData), .en(decoder_1_out8), .Q(register_8_q), .clk(Clock), .clr(Reset));
  Register #(.width(32)) register_9 (.D(WriteData), .en(decoder_1_out9), .Q(register_9_q), .clk(Clock), .clr(Reset));
  Register #(.width(32)) register_10 (.D(WriteData), .en(decoder_1_out10), .Q(register_10_q), .clk(Clock), .clr(Reset));
  Register #(.width(32)) register_11 (.D(WriteData), .en(decoder_1_out11), .Q(register_11_q), .clk(Clock), .clr(Reset));
  Register #(.width(32)) register_12 (.D(WriteData), .en(decoder_1_out12), .Q(register_12_q), .clk(Clock), .clr(Reset));
  Register #(.width(32)) register_13 (.D(WriteData), .en(decoder_1_out13), .Q(register_13_q), .clk(Clock), .clr(Reset));
  Register #(.width(32)) register_14 (.D(WriteData), .en(decoder_1_out14), .Q(register_14_q), .clk(Clock), .clr(Reset));
  Register #(.width(32)) register_15 (.D(WriteData), .en(decoder_1_out15), .Q(register_15_q), .clk(Clock), .clr(Reset));
  Register #(.width(32)) register_16 (.D(WriteData), .en(decoder_1_out16), .Q(register_16_q), .clk(Clock), .clr(Reset));
  Register #(.width(32)) register_17 (.D(WriteData), .en(decoder_1_out17), .Q(register_17_q), .clk(Clock), .clr(Reset));
  Register #(.width(32)) register_18 (.D(WriteData), .en(decoder_1_out18), .Q(register_18_q), .clk(Clock), .clr(Reset));
  Register #(.width(32)) register_19 (.D(WriteData), .en(decoder_1_out19), .Q(register_19_q), .clk(Clock), .clr(Reset));
  Register #(.width(32)) register_20 (.D(WriteData), .en(decoder_1_out20), .Q(register_20_q), .clk(Clock), .clr(Reset));
  Register #(.width(32)) register_21 (.D(WriteData), .en(decoder_1_out21), .Q(register_21_q), .clk(Clock), .clr(Reset));
  Register #(.width(32)) register_22 (.D(WriteData), .en(decoder_1_out22), .Q(register_22_q), .clk(Clock), .clr(Reset));
  Register #(.width(32)) register_23 (.D(WriteData), .en(decoder_1_out23), .Q(register_23_q), .clk(Clock), .clr(Reset));
  Register #(.width(32)) register_24 (.D(WriteData), .en(decoder_1_out24), .Q(register_24_q), .clk(Clock), .clr(Reset));
  Register #(.width(32)) register_25 (.D(WriteData), .en(decoder_1_out25), .Q(register_25_q), .clk(Clock), .clr(Reset));
  Register #(.width(32)) register_26 (.D(WriteData), .en(decoder_1_out26), .Q(register_26_q), .clk(Clock), .clr(Reset));
  Register #(.width(32)) register_27 (.D(WriteData), .en(decoder_1_out27), .Q(register_27_q), .clk(Clock), .clr(Reset));
  Register #(.width(32)) register_28 (.D(WriteData), .en(decoder_1_out28), .Q(register_28_q), .clk(Clock), .clr(Reset));
  Register #(.width(32)) register_29 (.D(WriteData), .en(decoder_1_out29), .Q(register_29_q), .clk(Clock), .clr(Reset));
  Register #(.width(32)) register_30 (.D(WriteData), .en(decoder_1_out30), .Q(register_30_q), .clk(Clock), .clr(Reset));
  Register #(.width(32)) register_31 (.D(WriteData), .en(decoder_1_out31), .Q(register_31_q), .clk(Clock), .clr(Reset));
  Multiplexer #(.select(5), .width(32), .disabled(0), .enable("false")) multiplexer_1 (
    .in0(R0_q), .in1(register_1_q), .in2(register_2_q), .in3(register_3_q), .in4(register_4_q),
    .in5(register_5_q), .in6(register_6_q), .in7(register_7_q), .in8(register_8_q), .in9(register_9_q),
    .in10(register_10_q), .in11(register_11_q), .in12(register_12_q), .in13(register_13_q),
    .in14(register_14_q), .in15(register_15_q), .in16(register_16_q), .in17(register_17_q),
    .in18(register_18_q), .in19(register_19_q), .in20(register_20_q), .in21(register_21_q),
    .in22(register_22_q), .in23(register_23_q), .in24(register_24_q), .in25(register_25_q),
    .in26(register_26_q), .in27(register_27_q), .in28(register_28_q), .in29(register_29_q),
    .in30(register_30_q), .in31(register_31_q), .out(ReadData1), .sel(ReadRegister1));
  Multiplexer #(.select(5), .width(32), .disabled(0), .enable("false")) multiplexer_2 (
    .in0(R0_q), .in1(register_1_q), .in2(register_2_q), .in3(register_3_q), .in4(register_4_q),
    .in5(register_5_q), .in6(register_6_q), .in7(register_7_q), .in8(register_8_q), .in9(register_9_q),
    .in10(register_10_q), .in11(register_11_q), .in12(register_12_q), .in13(register_13_q),
    .in14(register_14_q), .in15(register_15_q), .in16(register_16_q), .in17(register_17_q),
    .in18(register_18_q), .in19(register_19_q), .in20(register_20_q), .in21(register_21_q),
    .in22(register_22_q), .in23(register_23_q), .in24(register_24_q), .in25(register_25_q),
    .in26(register_26_q), .in27(register_27_q), .in28(register_28_q), .in29(register_29_q),
    .in30(register_30_q), .in31(register_31_q), .out(ReadData2), .sel(ReadRegister2));
endmodule

module ALU (
  input  [31:0] op1,
  input  [31:0] op2,
  input  [2:0] operation,
  output Zero,
  output [31:0] Result
);

  wire bitselector_1_out;
  wire [31:0] adder_1_out, and_1_out, bit_extender_1_out, multiplexer_1_out, not_1_out, or_1_out;

  Multiplexer #(.width(32), .disabled(0), .enable("false")) multiplexer_1 (
    .in0(op2), .in1(not_1_out), .out(multiplexer_1_out), .sel(operation[2]));
  assign not_1_out = ~op2;  // NOT_Gate not_1, 32 bits wide
  assign and_1_out = op1 & multiplexer_1_out;  // AND_Gate and_1, 32 bits wide
  assign or_1_out = op1 | multiplexer_1_out;  // OR_Gate or_1, 32 bits wide
  Adder #(.width(32)) adder_1 (.a(op1), .b(multiplexer_1_out), .out(adder_1_out), .cin(operation[2]));  // open: cout
  BitSelector #(.width(32)) bitselector_1 (.in(adder_1_out), .out(bitselector_1_out), .sel({5{1'b1}}));
  assign bit_extender_1_out = {{31{1'b0}}, bitselector_1_out};  // Bit_Extender bit_extender_1
  Multiplexer #(.select(2), .width(32), .disabled(0), .enable("false")) multiplexer_2 (
    .in0(and_1_out), .in1(or_1_out), .in2(adder_1_out), .in3(bit_extender_1_out), .out(Result),
    .sel(operation[1:0]));
  Comparator #(.width(32)) comparator_1 (.a({32{1'b0}}), .b(Result), .eq(Zero));  // open: gt, lt

  // Notes on the sheet:
  //   111: SLT
  //   000: op1 and op2
  //   001: op1 or op2
  //   010: op1 + op2
  //   110: op1 - op2
  //   Seleciona o bit de sinal
endmodule

module ControlPath (
  input  [5:0] Opcode,
  output Jump,
  output RegDst,
  output ALUSrc,
  output MemToReg,
  output RegWrite,
  output MemRead,
  output MemWrite,
  output Branch,
  output [1:0] ALUop
);

  wire and_5_out, and_6_out;

  // Probe on Opcode
  and and_1 (ALUop[1], ~Opcode[5], ~Opcode[4], ~Opcode[3], ~Opcode[2], ~Opcode[1], ~Opcode[0]);  // AND_Gate
  and and_2 (MemRead, Opcode[5], ~Opcode[4], ~Opcode[3], ~Opcode[2], Opcode[1], Opcode[0]);  // AND_Gate
  and and_3 (MemWrite, Opcode[5], ~Opcode[4], Opcode[3], ~Opcode[2], Opcode[1], Opcode[0]);  // AND_Gate
  and and_4 (ALUop[0], ~Opcode[5], ~Opcode[4], ~Opcode[3], Opcode[2], ~Opcode[1], ~Opcode[0]);  // AND_Gate
  and and_5 (and_5_out, ~Opcode[5], ~Opcode[4], Opcode[3], ~Opcode[2], ~Opcode[1], Opcode[0]);  // AND_Gate
  and and_6 (and_6_out, ~Opcode[5], ~Opcode[4], ~Opcode[3], ~Opcode[2], Opcode[1], ~Opcode[0]);  // AND_Gate
  not not_1 (Jump, and_6_out);
  or or_1 (ALUSrc, MemRead, and_5_out, MemWrite);
  not not_2 (MemToReg, MemRead);
  or or_2 (RegWrite, ALUop[1], and_5_out, MemRead);

  assign Branch = ALUop[0];
  assign RegDst = ALUop[1];

  // Notes on the sheet:
  //   R-type
  //   lw (35)
  //   sw (43)
  //   beq (4)
  //   addiu (9)
  //   j (2)
endmodule

module ALUControl (
  input  [1:0] ALUop,
  input  [5:0] funct,
  output [2:0] operation
);

  wire and_1_out, or_1_out;

  or or_1 (or_1_out, funct[3], funct[0]);
  and and_1 (and_1_out, ALUop[1], funct[1]);
  or or_2 (operation[2], ALUop[0], and_1_out);
  or or_3 (operation[1], ~ALUop[1], ~funct[2]);  // OR_Gate
  and and_2 (operation[0], ALUop[1], or_1_out);
endmodule
