// Logisim project memory256x32.circ as structural Verilog: 1 circuit, main circuit main
module main (
  input  [7:0] Address,
  input  [31:0] Data_in,
  input  [3:0] wbe,
  output [31:0] Data_out
);

  wire clk_out;

  Button clk (.out(clk_out));
  RAM #(.bus("separate")) ram_1 (
    .addr(Address), .din(Data_in[31:24]), .data(Data_out[31:24]), .str(wbe[3]), .clk(clk_out));  // open: sel, ld, clr
  // Probe on Data_out
  RAM #(.bus("separate")) ram_2 (
    .addr(Address), .din(Data_in[23:16]), .data(Data_out[23:16]), .str(wbe[2]), .clk(clk_out));  // open: sel, ld, clr
  RAM #(.bus("separate")) ram_3 (
    .addr(Address), .din(Data_in[15:8]), .data(Data_out[15:8]), .str(wbe[1]), .clk(clk_out));  // open: sel, ld, clr
  RAM #(.bus("separate")) ram_4 (
    .addr(Address), .din(Data_in[7:0]), .data(Data_out[7:0]), .str(wbe[0]), .clk(clk_out));  // open: sel, ld, clr

  // Notes on the sheet:
  //   Byte 3
  //   Byte 2
  //   Byte 1
  //   Byte 0
  //   Byte 3
  //   Byte 3
  //   Byte 2
  //   Byte 1
  //   Byte 0
  //   Memory 256x32
  //   Byte 2
  //   Byte 1
  //   Byte 0
endmodule
