// Logisim project Neander_DataPath_v2.circ as structural Verilog: 2 circuits, main circuit main
module main (
  input  incPC,
  input  wrPC,
  input  srcMAR,
  input  wrMAR,
  input  write,
  input  read,
  input  wrDFM,
  input  wrIR,
  input  wrAC,
  input  wrDTM,
  input  [2:0] opULA,
  input  wrNZ,
  output N,
  output Z
);

  wire Clock, Reset;
  wire [1:0] ula_1_z;
  wire [7:0] AC_q, adder_1_out, DFM_q, DTM_q, IR_q, MAR_q, multiplexer_1_out, multiplexer_2_out, PC_q,
       ram_1_data, ula_1_result;

  Button u_Reset (.out(Reset));
  Button u_Clock (.out(Clock));
  Multiplexer #(.width(8), .enable("false")) multiplexer_1 (
    .in0(adder_1_out), .in1(DFM_q), .out(multiplexer_1_out), .sel(incPC));
  Register PC (.D(multiplexer_1_out), .en(wrPC), .Q(PC_q), .clk(Clock), .clr(Reset));
  Adder adder_1 (.a(8'h1), .b(PC_q), .out(adder_1_out), .cin(1'b0));  // open: cout
  Register AC (.D(ula_1_result), .en(wrAC), .Q(AC_q), .clk(Clock), .clr(Reset));
  ULA ula_1 (.A(AC_q), .B(DFM_q), .Result(ula_1_result), .N(ula_1_z[1]), .Z(ula_1_z[0]), .opULA(opULA));
  Multiplexer #(.width(8), .enable("false")) multiplexer_2 (
    .in0(PC_q), .in1(DFM_q), .out(multiplexer_2_out), .sel(srcMAR));
  Register #(.width(2)) Flags__ZN (.D(ula_1_z), .en(wrNZ), .Q({Z, N}), .clk(Clock), .clr(Reset));
  Register MAR (.D(multiplexer_2_out), .en(wrMAR), .Q(MAR_q), .clk(Clock), .clr(Reset));
  Register DTM (.D(AC_q), .en(wrDTM), .Q(DTM_q), .clk(Clock), .clr(Reset));
  RAM #(.bus("separate")) ram_1 (
    .addr(MAR_q), .din(DTM_q), .data(ram_1_data), .str(write), .sel(1'b1), .clk(Clock), .ld(read), .clr(1'b0));
  Register DFM (.D(ram_1_data), .en(wrDFM), .Q(DFM_q), .clk(Clock), .clr(Reset));
  Register IR (.D(DFM_q), .en(wrIR), .Q(IR_q), .clk(Clock), .clr(Reset));

  // Notes on the sheet:
  //   ULA
  //   000 - passa B
  //   001 - A + B
  //   010 - not A
  //   011 - A and B
  //   100 - A or B
  //   Bloco de controle
endmodule

module ULA (
  input  [7:0] A,
  input  [7:0] B,
  input  [2:0] opULA,
  output N,
  output Z,
  output [7:0] Result
);

  wire [7:0] adder_1_out, and_1_out, not_1_out, or_1_out;

  Adder adder_1 (.a(A), .b(B), .out(adder_1_out), .cin(1'b0));  // open: cout
  assign not_1_out = ~A;  // NOT_Gate not_1, 8 bits wide
  assign and_1_out = A & B;  // AND_Gate and_1, 8 bits wide
  assign or_1_out = A | B;  // OR_Gate or_1, 8 bits wide
  Multiplexer #(.select(3), .width(8), .enable("false")) multiplexer_1 (
    .in0(B), .in1(adder_1_out), .in2(not_1_out), .in3(and_1_out), .in4(or_1_out), .in5(A), .in6({8{1'b0}}),
    .in7({8{1'b0}}), .out({N, Result[6:0]}), .sel(opULA));
  and and_2 (Z, ~N, ~Result[6], ~Result[5], ~Result[4], ~Result[3], ~Result[2], ~Result[1], ~Result[0]);  // AND_Gate

  assign Result[7] = N;

  // Notes on the sheet:
  //   000 - passa B
  //   001 - A + B
  //   010 - not A
  //   011 - A and B
  //   100 - A or B
endmodule
