// Logisim project Neander_v4.circ as structural Verilog: 6 circuits, main circuit Neander
module Neander (
);

  wire bloco_de_controle_1_srcmar, bloco_de_controle_1_srcpc, bloco_de_controle_1_wrac,
       bloco_de_controle_1_wrdfm, bloco_de_controle_1_wrdtm, bloco_de_controle_1_wrir,
       bloco_de_controle_1_wrmar, bloco_de_controle_1_wrmem, bloco_de_controle_1_wrnz,
       bloco_de_controle_1_wrpc, Clock, Clock_out, Reset;
  wire [1:0] Flags__ZN_q, ula_1_z;
  wire [2:0] bloco_de_controle_1_opula;
  wire [3:0] bloco_de_controle_1_estado_atual__ea;
  wire [7:0] AC_q, adder_1_out, DFM_q, DTM_q, IR_q, MAR_q, multiplexer_1_out, multiplexer_2_out, PC_q,
       ram_1_data, ula_1_result;

  // Probe on bloco_de_controle_1_estado_atual__ea
  Bloco_de_Controle bloco_de_controle_1 (
    .srcPC(bloco_de_controle_1_srcpc), .wrPC(bloco_de_controle_1_wrpc), .srcMAR(bloco_de_controle_1_srcmar),
    .wrMAR(bloco_de_controle_1_wrmar), .wrMEM(bloco_de_controle_1_wrmem), .wrDFM(bloco_de_controle_1_wrdfm),
    .wrIR(bloco_de_controle_1_wrir), .N(Flags__ZN_q[1]), .Z(Flags__ZN_q[0]),
    .opULA(bloco_de_controle_1_opula), .wrNZ(bloco_de_controle_1_wrnz), .wrAC(bloco_de_controle_1_wrac),
    .wrDTM(bloco_de_controle_1_wrdtm), .Estado_Atual__EA(bloco_de_controle_1_estado_atual__ea),
    .Reset(Reset), .Clock(Clock_out), .IR(IR_q));  // open: Proximo_estado__PE
  Button u_Reset (.out(Reset));
  Clock u_Clock (.out(Clock_out));
  Multiplexer #(.width(8), .enable("false")) multiplexer_1 (
    .in0(adder_1_out), .in1(DFM_q), .out(multiplexer_1_out), .sel(bloco_de_controle_1_srcpc));
  not not_1 (Clock, Clock_out);
  Register PC (.D(multiplexer_1_out), .en(bloco_de_controle_1_wrpc), .Q(PC_q), .clk(Clock), .clr(Reset));
  ULA ula_1 (
    .A(AC_q), .B(DFM_q), .Result(ula_1_result), .N(ula_1_z[1]), .Z(ula_1_z[0]),
    .opULA(bloco_de_controle_1_opula));
  Adder adder_1 (.a(8'h1), .b(PC_q), .out(adder_1_out), .cin(1'b0));  // open: cout
  Register AC (.D(ula_1_result), .en(bloco_de_controle_1_wrac), .Q(AC_q), .clk(Clock), .clr(Reset));
  Multiplexer #(.width(8), .enable("false")) multiplexer_2 (
    .in0(PC_q), .in1(DFM_q), .out(multiplexer_2_out), .sel(bloco_de_controle_1_srcmar));
  Register #(.width(2)) Flags__ZN (
    .D(ula_1_z), .en(bloco_de_controle_1_wrnz), .Q(Flags__ZN_q), .clk(Clock), .clr(Reset));
  Register MAR (.D(multiplexer_2_out), .en(bloco_de_controle_1_wrmar), .Q(MAR_q), .clk(Clock), .clr(Reset));
  Register DTM (.D(AC_q), .en(bloco_de_controle_1_wrdtm), .Q(DTM_q), .clk(Clock), .clr(Reset));
  RAM #(.bus("separate")) ram_1 (
    .addr(MAR_q), .din(DTM_q), .data(ram_1_data), .str(bloco_de_controle_1_wrmem), .sel(1'b1), .clk(Clock),
    .ld(1'b1), .clr(1'b0));
  Register DFM (.D(ram_1_data), .en(bloco_de_controle_1_wrdfm), .Q(DFM_q), .clk(Clock), .clr(Reset));
  Register IR (.D(DFM_q), .en(bloco_de_controle_1_wrir), .Q(IR_q), .clk(Clock), .clr(Reset));
endmodule

module ULA (
  input  [7:0] A,
  input  [7:0] B,
  input  [2:0] opULA,
  output N,
  output Z,
  output [7:0] Result
);

  wire [7:0] adder_1_out, and_1_out, not_1_out, or_1_out;

  Adder adder_1 (.a(A), .b(B), .out(adder_1_out), .cin(1'b0));  // open: cout
  assign not_1_out = ~A;  // NOT_Gate not_1, 8 bits wide
  assign and_1_out = A & B;  // AND_Gate and_1, 8 bits wide
  assign or_1_out = A | B;  // OR_Gate or_1, 8 bits wide
  Multiplexer #(.select(3), .width(8), .enable("false")) multiplexer_1 (
    .in0(B), .in1(adder_1_out), .in2(not_1_out), .in3(and_1_out), .in4(or_1_out), .in5(A), .in6({8{1'b0}}),
    .in7({8{1'b0}}), .out({N, Result[6:0]}), .sel(opULA));
  and and_2 (Z, ~N, ~Result[6], ~Result[5], ~Result[4], ~Result[3], ~Result[2], ~Result[1], ~Result[0]);  // AND_Gate

  assign Result[7] = N;
endmodule

// Bloco de controle
module Bloco_de_Controle (
  input  N,
  input  Z,
  input  Reset,
  input  Clock,
  input  [7:0] IR,
  output [3:0] Estado_Atual__EA,
  output [3:0] Proximo_estado__PE,
  output srcPC,
  output wrPC,
  output srcMAR,
  output wrMAR,
  output wrMEM,
  output wrDFM,
  output wrIR,
  output [2:0] opULA,
  output wrNZ,
  output wrAC,
  output wrDTM
);

  Proximo_Estado proximo_estado_1 (
    .s3(Estado_Atual__EA[3]), .s2(Estado_Atual__EA[2]), .s1(Estado_Atual__EA[1]), .s0(Estado_Atual__EA[0]),
    .IR7(IR[7]), .IR6(IR[6]), .IR5(IR[5]), .IR4(IR[4]), .Z(Z), .N(N), .PE3(Proximo_estado__PE[3]),
    .PE2(Proximo_estado__PE[2]), .PE1(Proximo_estado__PE[1]), .PE0(Proximo_estado__PE[0]));
  Register #(.width(4)) Registrador_de_estado (
    .D(Proximo_estado__PE), .en(1'b1), .Q(Estado_Atual__EA), .clk(Clock), .clr(Reset));
  ULA_Ctrl Controle_da_ULA (
    .IR7(IR[7]), .IR6(IR[6]), .IR5(IR[5]), .IR4(IR[4]), .opULA2(opULA[2]), .opULA1(opULA[1]),
    .opULA0(opULA[0]));
  Sinais Sinais_de_controle (
    .s3(Estado_Atual__EA[3]), .s2(Estado_Atual__EA[2]), .s1(Estado_Atual__EA[1]), .s0(Estado_Atual__EA[0]),
    .PC_Src(srcPC), .wrPC(wrPC), .REM_Src(srcMAR), .wrREM(wrMAR), .wrMEM(wrMEM), .wrDFM(wrDFM), .wrIR(wrIR),
    .wrNZ(wrNZ), .wrAC(wrAC), .wrDTM(wrDTM));

  // Notes on the sheet:
  //   Máquina de Moore
endmodule

module Sinais (
  input  s3,
  input  s2,
  input  s1,
  input  s0,
  output PC_Src,
  output wrPC,
  output REM_Src,
  output wrREM,
  output wrMEM,
  output wrDFM,
  output wrIR,
  output wrNZ,
  output wrAC,
  output wrDTM
);

  wire and_3_out, and_4_out, and_5_out, and_6_out, and_7_out, and_8_out, and_10_out, and_11_out, not_1_out,
       not_2_out, not_3_out, not_4_out, not_5_out, not_6_out, not_7_out, not_8_out, not_9_out, not_10_out,
       not_11_out, not_12_out, not_13_out, not_14_out, not_15_out, not_16_out, not_17_out, not_18_out,
       not_19_out, not_20_out, not_21_out, not_22_out, not_23_out, not_24_out, not_25_out, not_26_out,
       not_27_out;

  not not_1 (not_1_out, s3);
  not not_2 (not_2_out, s2);
  not not_3 (not_3_out, s1);
  not not_4 (not_4_out, s3);
  not not_5 (not_5_out, s1);
  not not_6 (not_6_out, s0);
  not not_7 (not_7_out, s2);
  not not_8 (not_8_out, s0);
  not not_9 (not_9_out, s3);
  not not_10 (not_10_out, s2);
  not not_11 (not_11_out, s1);
  not not_12 (not_12_out, s3);
  not not_13 (not_13_out, s0);
  not not_14 (not_14_out, s2);
  not not_15 (not_15_out, s1);
  not not_16 (not_16_out, s0);
  not not_17 (not_17_out, s3);
  not not_18 (not_18_out, s2);
  not not_19 (not_19_out, s0);
  not not_20 (not_20_out, s3);
  not not_21 (not_21_out, s3);
  not not_22 (not_22_out, s2);
  and and_1 (wrNZ, s3, not_23_out, not_24_out);
  not not_23 (not_23_out, s2);
  not not_24 (not_24_out, s1);
  not not_25 (not_25_out, s2);
  and and_2 (wrAC, s3, not_25_out, not_26_out);
  not not_26 (not_26_out, s1);
  not not_27 (not_27_out, s2);
  and and_3 (and_3_out, not_1_out, not_2_out, not_3_out, s0);
  and and_4 (and_4_out, not_4_out, s2, not_5_out, not_6_out);
  or or_1 (wrPC, and_3_out, and_4_out, and_5_out);
  and and_5 (and_5_out, s3, not_7_out, s1, not_8_out);
  and and_6 (and_6_out, not_9_out, not_10_out, not_11_out, s0);
  and and_7 (and_7_out, not_12_out, s2, not_13_out);
  or or_2 (wrREM, and_6_out, and_7_out, and_8_out);
  and and_8 (and_8_out, s3, not_14_out, s1, s0);
  and and_9 (wrMEM, s3, s2, not_15_out, not_16_out);
  and and_10 (and_10_out, not_17_out, not_18_out, s1, not_19_out);
  or or_3 (wrDFM, and_10_out, and_11_out);
  and and_11 (and_11_out, not_20_out, s2, s0);
  and and_12 (wrIR, not_21_out, not_22_out, s1, s0);
  and and_13 (wrDTM, s3, not_27_out, s1, s0);

  assign PC_Src = s1;
  assign REM_Src = s1;
endmodule

module ULA_Ctrl (
  input  IR7,
  input  IR6,
  input  IR5,
  input  IR4,
  output opULA2,
  output opULA1,
  output opULA0
);

  wire and_1_out, and_2_out, and_3_out, and_4_out, and_5_out, and_6_out, not_1_out, not_2_out, not_3_out,
       not_4_out, not_5_out, not_6_out;

  not not_1 (not_1_out, IR5);
  and and_1 (and_1_out, not_1_out, not_2_out);
  not not_2 (not_2_out, IR4);
  not not_3 (not_3_out, IR7);
  not not_4 (not_4_out, IR5);
  and and_2 (and_2_out, not_3_out, not_4_out, IR4);
  and and_3 (and_3_out, IR6, IR4);
  and and_4 (and_4_out, IR6, IR5);
  and and_5 (and_5_out, IR7, not_5_out, not_6_out);
  not not_5 (not_5_out, IR5);
  not not_6 (not_6_out, IR4);
  and and_6 (and_6_out, IR7, IR5, IR4);
  or or_1 (opULA0, IR4, IR7);
  or or_2 (opULA2, and_1_out, IR7);
  or or_3 (opULA1, and_2_out, and_3_out, and_4_out, and_5_out, and_6_out);
endmodule

// Próximo estado
module Proximo_Estado (
  input  s3,
  input  s2,
  input  s1,
  input  s0,
  input  IR7,
  input  IR6,
  input  IR5,
  input  IR4,
  input  Z,
  input  N,
  output PE3,
  output PE2,
  output PE1,
  output PE0
);

  wire and_1_out, and_2_out, and_3_out, and_4_out, and_5_out, and_6_out, and_7_out, and_8_out, and_9_out,
       and_10_out, and_11_out, and_12_out, and_13_out, and_14_out, and_15_out, and_16_out, and_17_out,
       and_18_out, and_19_out, and_20_out, and_21_out, and_22_out, and_23_out, and_24_out, and_25_out,
       and_26_out, and_27_out, and_28_out, and_29_out, and_30_out, and_31_out, and_32_out, and_33_out,
       not_1_out, not_2_out, not_3_out, not_4_out, not_5_out, not_6_out, not_7_out, not_8_out, not_9_out,
       not_10_out, not_11_out, not_12_out, not_13_out, not_14_out, not_15_out, not_16_out, not_17_out,
       not_18_out, not_19_out, not_20_out, not_21_out, not_22_out, not_23_out, not_24_out, not_25_out,
       not_26_out, not_27_out, not_28_out, not_29_out, not_30_out, not_31_out, not_32_out, not_33_out,
       not_34_out, not_35_out, not_36_out, not_37_out, not_38_out, not_39_out, not_40_out, not_41_out,
       not_42_out, not_43_out, not_44_out, not_45_out, not_46_out, not_47_out, not_48_out, not_49_out,
       not_50_out, not_51_out, not_52_out, not_53_out, not_54_out, not_55_out, not_56_out, not_57_out,
       not_58_out, not_59_out, not_60_out, not_61_out, not_62_out, not_63_out, not_64_out, not_65_out,
       not_66_out;

  not not_1 (not_1_out, IR7);
  not not_2 (not_2_out, IR4);
  not not_3 (not_3_out, IR7);
  not not_4 (not_4_out, IR6);
  not not_5 (not_5_out, IR5);
  not not_6 (not_6_out, IR6);
  not not_7 (not_7_out, IR5);
  not not_8 (not_8_out, IR4);
  not not_9 (not_9_out, IR6);
  not not_10 (not_10_out, IR5);
  not not_11 (not_11_out, IR6);
  not not_12 (not_12_out, IR4);
  not not_13 (not_13_out, s2);
  not not_14 (not_14_out, s2);
  not not_15 (not_15_out, IR6);
  not not_16 (not_16_out, s2);
  not not_17 (not_17_out, IR5);
  not not_18 (not_18_out, s2);
  not not_19 (not_19_out, s3);
  not not_20 (not_20_out, s0);
  not not_21 (not_21_out, IR7);
  not not_22 (not_22_out, s3);
  not not_23 (not_23_out, s0);
  not not_24 (not_24_out, s3);
  not not_25 (not_25_out, s0);
  not not_26 (not_26_out, IR7);
  not not_27 (not_27_out, s3);
  not not_28 (not_28_out, s0);
  not not_29 (not_29_out, s3);
  not not_30 (not_30_out, s1);
  not not_31 (not_31_out, s3);
  not not_32 (not_32_out, s1);
  not not_33 (not_33_out, s3);
  not not_34 (not_34_out, s0);
  not not_35 (not_35_out, IR5);
  not not_36 (not_36_out, IR4);
  not not_37 (not_37_out, s1);
  not not_38 (not_38_out, IR7);
  not not_39 (not_39_out, IR4);
  not not_40 (not_40_out, s1);
  not not_41 (not_41_out, Z);
  not not_42 (not_42_out, s1);
  not not_43 (not_43_out, N);
  not not_44 (not_44_out, s0);
  not not_45 (not_45_out, s3);
  not not_46 (not_46_out, s1);
  not not_47 (not_47_out, s3);
  not not_48 (not_48_out, s0);
  not not_49 (not_49_out, s3);
  not not_50 (not_50_out, s2);
  not not_51 (not_51_out, IR7);
  not not_52 (not_52_out, IR6);
  not not_53 (not_53_out, IR5);
  not not_54 (not_54_out, IR4);
  not not_55 (not_55_out, s3);
  not not_56 (not_56_out, s2);
  not not_57 (not_57_out, IR7);
  not not_58 (not_58_out, IR4);
  not not_59 (not_59_out, s3);
  not not_60 (not_60_out, s2);
  not not_61 (not_61_out, s1);
  not not_62 (not_62_out, IR7);
  not not_63 (not_63_out, IR6);
  not not_64 (not_64_out, IR5);
  not not_65 (not_65_out, s1);
  and and_1 (and_1_out, s1, s0, not_1_out, IR6, IR5, not_2_out);
  and and_2 (and_2_out, s1, s0, IR7, IR6, IR5, IR4);
  and and_3 (and_3_out, s2, s0, not_3_out, not_4_out, not_5_out, IR4);
  and and_4 (and_4_out, s2, s0, IR7, not_6_out, not_7_out, not_8_out);
  and and_5 (and_5_out, s2, s0, IR7, not_9_out, not_10_out, N);
  and and_6 (and_6_out, s2, s0, IR7, not_11_out, not_12_out, Z);
  and and_7 (and_7_out, s2, s1, s0);
  and and_8 (and_8_out, s3, s1, s0);
  and and_9 (and_9_out, s3, s2, s0);
  and and_10 (and_10_out, not_13_out, s1, s0, IR4);
  and and_11 (and_11_out, not_14_out, s1, s0, not_15_out, IR5);
  and and_12 (and_12_out, not_16_out, s1, s0, IR6, not_17_out);
  and and_13 (and_13_out, not_18_out, s1, s0, IR7);
  and and_14 (and_14_out, not_19_out, s2, not_20_out, not_21_out, IR4);
  and and_15 (and_15_out, not_22_out, s2, not_23_out, IR4, N);
  and and_16 (and_16_out, not_24_out, s2, not_25_out, not_26_out, IR5);
  and and_17 (and_17_out, not_27_out, s2, not_28_out, IR5, Z);
  and and_18 (and_18_out, not_29_out, s2, not_30_out, IR5, IR4);
  and and_19 (and_19_out, not_31_out, s2, not_32_out, IR6);
  and and_20 (and_20_out, not_33_out, s2, not_34_out, IR7, not_35_out, not_36_out);
  and and_21 (and_21_out, s2, not_37_out, s0, not_38_out, not_39_out);
  and and_22 (and_22_out, s2, not_40_out, s0, IR5, not_41_out);
  and and_23 (and_23_out, s2, not_42_out, s0, IR7, IR4, not_43_out);
  and and_24 (and_24_out, s2, s1, not_44_out);
  and and_25 (and_25_out, s3, s1, s0);
  and and_26 (and_26_out, s3, s2, s0);
  and and_27 (and_27_out, not_45_out, not_46_out, s0);
  and and_28 (and_28_out, not_47_out, s1, not_48_out);
  not not_66 (not_66_out, s0);
  and and_29 (and_29_out, not_49_out, not_50_out, s1, not_51_out, not_52_out, not_53_out, not_54_out);
  and and_30 (and_30_out, not_55_out, not_56_out, s1, not_57_out, IR6, IR5, not_58_out);
  and and_31 (and_31_out, not_59_out, not_60_out, s1, IR7, IR6, IR5, IR4);
  and and_32 (and_32_out, s2, not_61_out, not_62_out, not_63_out, not_64_out, IR4);
  and and_33 (and_33_out, s3, not_65_out);
  or or_1 (PE3, and_1_out, and_2_out, and_3_out, and_4_out, and_5_out, and_6_out, and_7_out, and_8_out, and_9_out);
  or or_2 (PE1, and_27_out, and_28_out);
  or or_3 (PE0, not_66_out, and_29_out, and_30_out, and_31_out, and_32_out, and_33_out);
  or or_4 (PE2, and_10_out, and_11_out, and_12_out, and_13_out, and_14_out, and_15_out, and_16_out, and_17_out, and_18_out, and_19_out, and_20_out, and_21_out, and_22_out, and_23_out, and_24_out, and_25_out, and_26_out);
endmodule
